# Fritzing sketch wiring (saved by Fritzing 0.9.0b)
breadboards: 1

parts:
  Деталь1 = Arduino Nano (Rev3.0)
  RHT1 = Humidity and Temperature Sensor RHT03
  Деталь2 = Barometric Pressure Sensor - BMP085 Breakout
  R1 = Resistor [tolerance=±5% resistance=1k package=THT]
  Деталь3 = Arduino Ethernet Shield (Rev3)

nets:
  N1: Деталь1.D1/TX, Деталь3.TX/D1
  N2: Деталь1.D0/RX, Деталь3.RX/D0
  GND: Деталь1.GND, RHT1.GND_2, Деталь2.GND, Деталь3.GND
  N3: Деталь1.D3, RHT1.Data-signal, R1.Pin_1
  N4: Деталь1.D10, Деталь3.ETH_CS
  N5: Деталь1.D11/MOSI, Деталь3.PWM_D11
  N6: Деталь1.D12/MISO, Деталь3.SPI/D12
  5V: Деталь1.5V, RHT1.Vcc, R1.Pin_0, Деталь3.5V
  N7: Деталь1.A5, Деталь2.SCL
  N8: Деталь1.A4, Деталь2.SDA
  N9: Деталь1.AREF, Деталь3.AREF
  3V3: Деталь1.3V3, Деталь2.VCC
  N10: Деталь1.D13/SCK, Деталь3.SPI/D13
